// Logisim project ComputerCircuitry.circ as structural Verilog: 6 circuits, main circuit main
module main (
);

  wire AI, AO, BI, BO, CE, CF, CLK, CO;
  wire [2:0] counter_1_q;
  wire [3:0] _4LSB, alu_1_out_6, alu_1_out_6_2, program_counter_1_out_6, program_counter_1_out_6_2,
       register_1_q;
  wire [7:0] ADISPLAY, BDISPLAY, controlled_buffer_2_out, register_2_q;
  wire [7:4] BUS;
  wire [11:0] CTRL_WORD;

  Clock clock_1 (.out(CLK));
  Register #(.width(4)) register_1 (.D(_4LSB), .en(CTRL_WORD[4]), .Q(register_1_q), .clk(CLK));  // open: clr
  Hex_Digit_Display hex_digit_display_1 (.value(BUS));  // open: dp
  Hex_Digit_Display hex_digit_display_2 (.value(_4LSB));  // open: dp
  RAM #(.addrWidth(4), .bus("separate")) ram_1 (
    .addr(register_1_q), .din({BUS, _4LSB}), .data({BUS, _4LSB}), .str(CTRL_WORD[9]), .sel(1'b1), .clk(CLK),
    .ld(CTRL_WORD[8]));  // open: clr
  assign BUS = CTRL_WORD[2] ? 4'b0000 : 4'bz;  // Controlled_Buffer controlled_buffer_1
  // Probe on {BUS, _4LSB}
  Hex_Digit_Display hex_digit_display_3 (.value(program_counter_1_out_6_2));  // open: dp
  LED led_1 (.in(ADISPLAY[5]));
  LED led_2 (.in(ADISPLAY[4]));
  LED led_3 (.in(ADISPLAY[6]));
  LED led_4 (.in(ADISPLAY[7]));
  Hex_Digit_Display hex_digit_display_4 (.value(alu_1_out_6));  // open: dp
  Hex_Digit_Display hex_digit_display_5 (.value(alu_1_out_6_2));  // open: dp
  LED led_5 (.in(BDISPLAY[4]));
  LED led_6 (.in(BDISPLAY[5]));
  LED led_7 (.in(BDISPLAY[6]));
  LED led_8 (.in(BDISPLAY[7]));
  Hex_Digit_Display hex_digit_display_6 (.value(program_counter_1_out_6));  // open: dp
  LED led_9 (.in(ADISPLAY[0]));
  LED led_10 (.in(ADISPLAY[3]));
  LED led_11 (.in(ADISPLAY[2]));
  LED led_12 (.in(ADISPLAY[1]));
  ALU alu_1 (
    .in_1(ADISPLAY), .B(BDISPLAY), .in_3(CLK), .\ΣO (CTRL_WORD[11]), .SU(CTRL_WORD[10]),
    .out_7({BUS, _4LSB}), .out_6({alu_1_out_6_2, alu_1_out_6}), .CF(CF));
  LED led_13 (.in(BDISPLAY[2]));
  LED led_14 (.in(BDISPLAY[3]));
  LED led_15 (.in(BDISPLAY[1]));
  LED led_16 (.in(BDISPLAY[0]));
  Program_Counter program_counter_1 (
    .in_1(CTRL_WORD[6]), .in_2({BUS, _4LSB}), .in_3(CE), .in_4(CLK), .in_5(CO), .out_7({BUS, _4LSB}),
    .out_6({program_counter_1_out_6_2, program_counter_1_out_6}));
  Hex_Digit_Display hex_digit_display_7 (.value(ADISPLAY[7:4]));  // open: dp
  Hex_Digit_Display hex_digit_display_8 (.value(ADISPLAY[3:0]));  // open: dp
  Hex_Digit_Display hex_digit_display_9 (.value(BDISPLAY[3:0]));  // open: dp
  Hex_Digit_Display hex_digit_display_10 (.value(BDISPLAY[7:4]));  // open: dp
  Areg areg_1 (.in_1({BUS, _4LSB}), .load(AI), .Enable(AO), .out_6({BUS, _4LSB}), .in_3(CLK), .out_5(ADISPLAY));
  Breg breg_1 (.in_1(CLK), .in_3({BUS, _4LSB}), .out_5({BUS, _4LSB}), .in_2(BI), .in_4(BO), .out_6(BDISPLAY));
  Register register_2 (.D(controlled_buffer_2_out), .Q(register_2_q), .clk(CLK));  // open: en, clr
  assign controlled_buffer_2_out = CTRL_WORD[3] ? {BUS, _4LSB} : 8'bz;  // Controlled_Buffer controlled_buffer_2
  Counter #(.width(3), .max('h4)) counter_1 (.Q(counter_1_q), .clk(CLK));  // open: load, D, count, carry, clr
  assign _4LSB = CTRL_WORD[2] ? register_2_q[3:0] : 4'bz;  // Controlled_Buffer controlled_buffer_3
  ROM #(.addrWidth(7), .dataWidth(16)) rom_1 (
    .addr({register_2_q[7:4], counter_1_q}),
    .data({AI, AO, BI, BO, CTRL_WORD[11:8], CO, CTRL_WORD[6], CE, CTRL_WORD[4:0]}));  // open: sel

  // Other names for the same wires on the sheet: BUS[3:0] = _4LSB; IO = CTRL_WORD[2]; II = CTRL_WORD[3];
  //   MI = CTRL_WORD[4]; CTRL_WORD (some bits) = {AI, AO, BI, BO, CO, CE}; JMP = CTRL_WORD[6]; RO = CTRL_WORD[8];
  //   RI = CTRL_WORD[9]; SU = CTRL_WORD[10]; ΣO = CTRL_WORD[11]

  // Notes on the sheet:
  //   16x8 RAM
  //   contents of rom_1 (hex, n*v repeats v):
  //   90 128 6*0 90 128 14 8100 4*0 90 128 14 2100 8800 0 0 0 90 128 14 2100 8c00 0 0 0 90 128 14 140 4*0
  //   90 128 14 4200 4*0 90 128 8004
endmodule

module Areg (
  input  [7:0] in_1,
  input  load,
  input  in_3,
  input  Enable,
  output [7:0] out_5,
  output [7:0] out_6
);

  Register register_1 (.D(in_1), .en(load), .Q(out_5), .clk(in_3));  // open: clr
  assign out_6 = Enable ? out_5 : 8'bz;  // Controlled_Buffer controlled_buffer_1
endmodule

module Breg (
  input  in_1,
  input  in_2,
  input  [7:0] in_3,
  input  in_4,
  output [7:0] out_5,
  output [7:0] out_6
);

  Areg areg_1 (.in_1(in_3), .load(in_2), .Enable(in_4), .out_6(out_5), .in_3(in_1), .out_5(out_6));
endmodule

module ALU (
  input  [7:0] in_1,
  input  [7:0] B,
  input  in_3,
  input  \ΣO ,
  input  SU,
  output [7:0] out_6,
  output [7:0] out_7,
  output CF
);

  wire [7:0] xor_1_out;

  xor xor_1 (xor_1_out[0], B[0], SU);
  xor xor_2 (xor_1_out[1], B[1], SU);
  xor xor_3 (xor_1_out[2], B[2], SU);
  xor xor_4 (xor_1_out[3], B[3], SU);
  xor xor_5 (xor_1_out[4], B[4], SU);
  xor xor_6 (xor_1_out[5], B[5], SU);
  xor xor_7 (xor_1_out[6], B[6], SU);
  xor xor_8 (xor_1_out[7], B[7], SU);
  Adder adder_1 (.a(in_1), .b(xor_1_out), .out(out_6), .cin(SU), .cout(CF));
  assign out_7 = \ΣO  ? out_6 : 8'bz;  // Controlled_Buffer controlled_buffer_1

  // Notes on the sheet:
  //   A
endmodule

module Program_Counter (
  input  in_1,
  input  [7:0] in_2,
  input  in_3,
  input  in_4,
  input  in_5,
  output [7:0] out_6,
  output [7:0] out_7
);

  Counter counter_1 (.load(in_1), .D(in_2), .count(in_3), .Q(out_6), .clk(in_4));  // open: carry, clr
  assign out_7 = in_5 ? out_6 : 8'bz;  // Controlled_Buffer controlled_buffer_1
endmodule

module Instruction_Register (
  input  II,
  input  IO,
  input  CLK,
  input  [7:0] in_4,
  output [15:0] out_5,
  output [3:0] out_6
);

  wire [2:0] counter_1_q;
  wire [7:0] register_1_q;

  Register register_1 (.D(in_4), .Q(register_1_q), .clk(II));  // open: en, clr
  Counter #(.width(3), .max('h4)) counter_1 (.Q(counter_1_q), .clk(CLK));  // open: load, D, count, carry, clr
  assign out_6 = IO ? register_1_q[7:4] : 4'bz;  // Controlled_Buffer controlled_buffer_1
  ROM #(.addrWidth(7), .dataWidth(16)) rom_1 (.addr({register_1_q[3:0], counter_1_q}), .data(out_5));  // open: sel

  // Notes on the sheet:
  //   contents of rom_1 (hex, n*v repeats v):
  //   24 4a 6*0 24 4a 5 840 2040
endmodule
